# Fritzing sketch wiringDiagram (saved by Fritzing 0.9.1b)

parts:
  Part1 = FONA 808 Shield
  Part2 = Adafruit ADXL335 [part_number="Adafruit #163"]
  U1 = LIPO-110mAh [package=lipo-110]  # not connected
  BAT1 = Battery Holders [package=lipo-1100mAh]
  Part4 = Arduino Uno (Rev3) - ICSP
  Part6 = PowerBoost 500 Charger
  ANT1 = Antenna  # not connected
  ANT2 = Antenna
  U3 = Mini-360 DC-DC Buck converter [package=THT]

nets:
  N1: Part1.DTR, ANT2.antenna_lead
  N2: Part1.D8, Part1.Key
  N3: Part1.D7, Part1.Pwr
  N4: Part1.VIN, Part6.5.0V
  5V: Part1.5V, Part2.VIN
  N5: Part1.A0, Part2.ZOUT
  N6: Part1.A1, Part2.YOUT
  N7: Part1.A2, Part2.XOUT
  N8: Part1.A5, Part6.LBO
  GND: Part1.GND, BAT1.-, Part6.GND, U3.OUT-
  GND_2: Part2.GND, Part4.GND
  N9: BAT1.+, Part6.VBAT
  N10: Part6.USB, U3.OUT+

custom parts:
  FONA 808 Shield: Cellular + GPS tracking, all in one, for your Arduino? Oh yes! Introducing Adafruit FONA 808 GSM + GPS Shield, an all-in-one cellular phone module with that lets you add location-tracking, voice, text, SMS and data to your project, in Arduino shield format for easy use.
  Adafruit ADXL335: We've updated our favorite triple-axis accelerometer to now have an on-board 3.3V regulator - making it a perfect choice for interfacing with a 5V microcontroller such as the Arduino. This breakout comes with 3 analog outputs for X, Y and Z axis measurements on a 0.75"x0.75" breakout board. The ADXL335 is the latest and greatest from Analog Devices, known for their exceptional quality MEMS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
  PowerBoost 500 Charger: The PowerBoost 500C is a little DC/DC boost converter module that can be powered by any 3.7V LiIon/LiPoly battery, and convert the battery output to 5.2V DC for running your 5V projects. At its heart is a TPS61090 boost converter from TI. This boost converter chip has some really nice extras such as low battery detection, 2A internal switch, synchronous conversion, excellent efficiency, and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
  Mini-360 DC-DC Buck converter: Mini-360 DC-DC Buck converter. Tiny buck step down voltage converter, input voltage 4.75 to 23V output 1 to 17V adjustable. Available from ebay and the like.
